// Logisim project seq_circuit.circ as structural Verilog: 1 circuit, main circuit main
module main (
  input  x,
  input  y,
  output S
);

  wire clock_1_out, main_1_p3, main_1_p5;

  Clock clock_1 (.out(clock_1_out));
  // _1bit_full_adder_main main_1: pin names not known; wires that end beside it: x, y, main_1_p3, S, main_1_p5
  D_Flip_Flop d_ff_1 (.clk(clock_1_out), .D(main_1_p5), .Q(main_1_p3));  // open: Qn, preset, en, reset
endmodule
